# Fritzing sketch buzzer_example (saved by Fritzing 1.0.6)
breadboards: 1

parts:
  Part1 = Arduino Uno (Rev3)
  J1 = Piezo Speaker
  R1 = Rotary Potentiometer (Small) [maximum_resistance=10kΩ knob_status=50% power=0.5W package=THT]
  R2 = Resistor [tolerance=±5% power=0.25W resistance=220 package=THT]
  LED1 = LED - 5mm [color="Red (633nm)" current=0.030A package="5 mm [THT]"]
  R3 = Resistor [tolerance=±5% power=0.25W resistance=220 package=THT]

nets:
  N1: Part1.A0, R1.wiper
  N2: Part1.D9_PWM, LED1.anode
  N3: Part1.D11_PWM/MOSI, J1.pin2
  N4: Part1.5V, R1.leg2
  N5: Part1.GND, R1.leg1, R2.Pin_1, R3.Pin_1
  N6: J1.pin1, R2.Pin_0
  N7: LED1.cathode, R3.Pin_0

// code stored in the sketch: Untitled2.ino
const int buzzerPin = 11;
const int ledPin = 9;
const int potPin = A0;


void setup() {
  pinMode(buzzerPin,OUTPUT);
  pinMode(ledPin,OUTPUT);
  pinMode(potPin,INPUT);
}


void loop() {
  int deger=analogRead(potPin);
  digitalWrite(buzzerPin,HIGH);
  digitalWrite(ledPin,HIGH);
  delay(deger);
  digitalWrite(buzzerPin,LOW);
  digitalWrite(ledPin,LOW);
}
