# Fritzing sketch traffic_light (saved by Fritzing 1.0.6)
breadboards: 1

parts:
  traffic-light = Arduino Uno (Rev3)
  LED3_Cars = smd LED [color="Green (570nm)" package="0805 [SMD]"]
  LED2_Cars = smd LED [color="Yellow (585nm)" package="0805 [SMD]"]
  LED1_Cars = smd LED [color="Red (633nm)" package="0805 [SMD]"]
  LED2_Walker = smd LED [color="Green (570nm)" package="0805 [SMD]"]
  LED1_Walker = smd LED [color="Red (633nm)" package="0805 [SMD]"]
  R1 = Resistor [tolerance=±5% power=0.25W resistance=220 package=THT]
  R2 = Resistor [tolerance=±5% power=0.25W resistance=220 package=THT]
  R3 = Resistor [tolerance=±5% power=0.25W resistance=220 package=THT]
  R4 = Resistor [tolerance=±5% power=0.25W resistance=220 package=THT]
  R5 = Resistor [tolerance=±5% power=0.25W resistance=220 package=THT]

nets:
  N1: traffic-light.D9_PWM, LED1_Walker.anode
  N2: traffic-light.D10_PWM/SS, LED2_Walker.anode
  N3: traffic-light.D11_PWM/MOSI, LED1_Cars.anode
  N4: traffic-light.D12/MISO, LED2_Cars.anode
  N5: traffic-light.D13/SCK, LED3_Cars.anode
  N6: traffic-light.GND, R1.Pin_1, R2.Pin_1, R3.Pin_1, R4.Pin_1, R5.Pin_1
  N7: LED3_Cars.cathode, R5.Pin_0
  N8: LED2_Cars.cathode, R4.Pin_0
  N9: LED1_Cars.cathode, R3.Pin_0
  N10: LED2_Walker.cathode, R2.Pin_0
  N11: LED1_Walker.cathode, R1.Pin_0
